# Fritzing sketch project (saved by Fritzing 0.9.3b)
circuit board: 8.91403cm x 5.46869cm
circuit board: 2.23564cm x 2.44904cm
breadboards: 1

parts:
  Componente1 = Arduino Due (Rev2b)
  LCD1 = LCD screen
  R2 = Rotary Potentiometer (Small) [maximum_resistance=100kΩ package=THT]
  S1 = Reed switch [package=THT]
  R3 = Resistor [tolerance=±5% resistance=10k package=THT]
  R1 = Rotary Potentiometer (Small) [maximum_resistance=100kΩ package=THT]

nets:
  5V: Componente1.5V, LCD1.VDD, R2.leg1, S1.pin_2, R1.leg1
  GND: Componente1.GND, LCD1.VSS, LCD1.R/W, LCD1.LED-, R2.leg2, R3.Pin_1, R1.leg2
  N1: Componente1.D8_PWM, S1.pin_1, R3.Pin_0
  N2: Componente1.D2_PWM, LCD1.DB7
  N3: Componente1.D3_PWM, LCD1.DB6
  N4: Componente1.D4_PWM/SS1, LCD1.DB5
  N5: Componente1.D5_PWM, LCD1.DB4
  N6: Componente1.D6_PWM, LCD1.E
  N7: Componente1.D7_PWM, LCD1.RS
  N8: LCD1.V0, R1.wiper
  N9: LCD1.LED+, R2.wiper
